# Fritzing sketch fritzing (saved by Fritzing 0.7.12b)
breadboards: 1

parts:
  S1 = Pushbutton [package=THT]
  R1 = Resistor [tolerance=±5% resistance=220 package=THT]
  U1 = mystery part, 6 pins [chip_label=PIR]
  LED1 = LED - 5mm [color="Red (633nm)" package="5 mm [THT]"]
  LED2 = LED - 5mm [color="Green (565nm)" package="5 mm [THT]"]
  R2 = Resistor [tolerance=±5% resistance=220 package=THT]
  R3 = Resistor [tolerance=±5% resistance=220 package=THT]
  Arduino1 = Arduino
  Power_plug1 = Power plug
  K1 = Relay [part_number=FRS1B-S package=THT]
  S2 = Toggle Switch [package=THT]
  J1 = screw terminal, 3 pins
  D1 = Rectifier Diode [part_number=1N4001 package="300 mil [THT]"]
  Q1 = NPN-Transistor [package="TO92 [THT]"]
  R4 = Resistor [tolerance=±5% resistance=220 package=THT]
  R5 = Resistor [tolerance=±5% resistance=220 package=THT]
  R6 = Resistor [tolerance=±5% resistance=220 package=THT]
  LED3 = LED - 5mm [color="Red (633nm)" package="5 mm [THT]"]
  J2 = Screw terminal - 2 pins [package=THT]

nets (from the schematic view):
  5V: S1.leg0, U1.pin1, Arduino1.+5V, K1.COIL1, J1.pin3, D1.cathode, R6.Pin_0
  N1: S1.leg1, Arduino1.D5
  GND: R1.Pin_1, U1.pin2, Arduino1.GND, J1.pin1, Q1.E, R5.Pin_1
  N2: U1.pin3, Arduino1.D2
  N3: U1.pin4, U1.pin5
  N4: LED1.cathode, LED2.cathode
  N5: LED1.anode, R2.Pin_1
  N6: R3.Pin_0, Arduino1.D3
  N7: Arduino1.D6, J1.pin2, R4.Pin_0
  N8: Arduino1.VIN, S2.COM
  N9: Power_plug1.GND, S2.L2
  N10: K1.A, J2.pin1
  N11: K1.C1, K1.C2
  N12: K1.COIL2, D1.anode, Q1.C, LED3.cathode
  N13: K1.B, J2.pin2
  N14: Q1.B, R4.Pin_1, R5.Pin_0
  N15: R6.Pin_1, LED3.anode
